# Fritzing sketch pru_blink (saved by Fritzing 0.9.3b)
breadboards: 1

parts:
  BeagleBone1 = BeagleBone Black
  R1 = Resistor [tolerance=±5% resistance=470 package="0603 [SMD]"]
  LED1 = LED - 3mm [color="Red (633nm)" package="3 mm [THT]"]

nets:
  N1: BeagleBone1.no_name_yet#102, LED1.cathode
  N2: BeagleBone1.no_name_yet#111, R1.Pin_0
  N3: R1.Pin_1, LED1.anode

custom parts:
  BeagleBone Black: BeagleBone Black rev. A5B
